# Fritzing sketch ESP32_weather_station (saved by Fritzing 0.9.3b)
breadboards: 1

parts:
  S1 = Toggle Switch [package=THT]
  R2 = Resistor [tolerance=±5% resistance=22k package=THT]
  U1 = LuaNode32 / ESP32
  R3 = Resistor [tolerance=±5% resistance=10k package=THT]
  RHT1 = Humidity and Temperature Sensor RHT03

nets:
  N1: S1.COM, R2.Pin_1, U1.D22
  5V: S1.L2, U1.3V3, R3.Pin_0, RHT1.Vcc
  GND: R2.Pin_0, U1.GND, RHT1.GND_2
  N2: U1.D23, R3.Pin_1, RHT1.Data-signal

custom parts:
  LuaNode32 / ESP32: ESP32 based LuaNode32
