# Fritzing sketch ESP32_weather_station_1_2_0 (saved by Fritzing 0.9.3b)
breadboards: 1

parts:
  R2 = Resistor [tolerance=±5% resistance=22k package=THT]
  R3 = Resistor [tolerance=±5% resistance=10k package=THT]
  S1 = Pushbutton [package=THT]
  DHT1 = DHT22 Humidity and Temperature Sensor
  part = MH-Z19 CO2 sensor [part_number=MH-Z19]
  ESP32 = LuaNode32 / ESP32
  LED1 = LED - 5mm [color="Blue (525nm)" package="5 mm [THT]"]
  LED3 = LED - 5mm [color="Yellow (595nm)" package="5 mm [THT]"]
  LED2 = LED - 3mm [color="Red (633nm)" package="3 mm [THT]"]
  R4 = Resistor [tolerance=±5% resistance=470 package=THT]
  R5 = Resistor [tolerance=±5% resistance=470 package=THT]
  R6 = Resistor [tolerance=±5% resistance=470 package=THT]

nets:
  GND: R2.Pin_0, DHT1.GND, part.GND, ESP32.GND, R4.Pin_0, R5.Pin_0, R6.Pin_0
  N1: R2.Pin_1, S1.leg1, ESP32.D22
  3.3V: R3.Pin_0, S1.leg0, DHT1.VDD, ESP32.3V3
  N2: R3.Pin_1, DHT1.DATA, ESP32.D23
  N3: part.RX, ESP32.TX2
  N4: part.TX, ESP32.RX2
  5V: part.Vin, ESP32.Vin
  N5: ESP32.D33, LED3.anode
  N6: ESP32.D27, LED2.anode
  N7: ESP32.D13, LED1.anode
  N8: LED1.cathode, R6.Pin_1
  N9: LED3.cathode, R4.Pin_1
  N10: LED2.cathode, R5.Pin_1

custom parts:
  LuaNode32 / ESP32: ESP32 based LuaNode32
